# Fritzing sketch circuit (saved by Fritzing 0.9.5d)
breadboards: 1

parts:
  HC-SR04_Sensor_1 = HC-SR04 Ultrasonic Distance Sensor
  U1 = NodeMCU V1.0
  LED1 = smd LED [color="Red (633nm)" package="0805 [SMD]"]
  LED2 = smd LED [color="Green (555nm)" package="0805 [SMD]"]
  R1 = Resistor [tolerance=±5% resistance=2k package="0603 [SMD]"]
  R2 = Resistor [tolerance=±5% resistance=1.2k package="0603 [SMD]"]
  R3 = Resistor [tolerance=±5% resistance=220 package="0603 [SMD]"]
  R4 = Resistor [tolerance=±5% resistance=220 package="0603 [SMD]"]

nets:
  VCC: HC-SR04_Sensor_1.VCC, U1.Vin
  N1: HC-SR04_Sensor_1.TRIG, U1.D1
  N2: HC-SR04_Sensor_1.ECHO, R2.Pin_0
  GND: HC-SR04_Sensor_1.GND, U1.GND, R1.Pin_1
  N3: U1.D2, R1.Pin_0, R2.Pin_1
  N4: U1.3V3, R3.Pin_1, R4.Pin_1
  N5: U1.D5, LED2.cathode
  N6: U1.D6, LED1.cathode
  N7: LED1.anode, R4.Pin_0
  N8: LED2.anode, R3.Pin_0

custom parts:
  NodeMCU V1.0: ESP8266 based NodeMCU
