# Fritzing sketch display (saved by Fritzing 0.9.3b)
breadboards: 1

parts:
  U2 = NodeMCU V1.0
  Componente2 = LCD1602-I2C

nets:
  N1: U2.D1, Componente2.SCL
  N2: U2.D2, Componente2.SDA
  GND: U2.GND, Componente2.GND
  VIN: U2.Vin, Componente2.VCC

custom parts:
  NodeMCU V1.0: ESP8266 based NodeMCU
  LCD1602-I2C: A standard character display, usually with 2x16 characters. Comes in many colors with LCM1602 IIC attached.
