# Fritzing sketch entrance (saved by Fritzing 0.9.5d)
breadboards: 1

parts:
  U1 = NodeMCU V1.0
  Componente1 = RFID-RC522-v2
  S1 = Pushbutton [package="[THT]"]
  R1 = Resistor [tolerance=±1% resistance=10k package=THT]
  Componente2 = LCD1602-I2C

nets:
  N1: U1.D1, Componente2.SCL
  N2: U1.D2, Componente2.SDA
  N3: U1.D3, Componente1.RST
  3V3: U1.3V3, Componente1.3.3V
  GND: U1.GND, Componente1.GND, S1.Pin_3, S1.Pin_4, Componente2.GND
  N4: U1.D5, Componente1.SCK
  N5: U1.D6, Componente1.MISO
  N6: U1.D7, Componente1.MOSI
  N7: U1.D8, Componente1.SDA
  VIN: U1.Vin, R1.Pin_1, Componente2.VCC
  N8: U1.RST, S1.Pin_1, S1.Pin_2, R1.Pin_0

custom parts:
  NodeMCU V1.0: ESP8266 based NodeMCU
  RFID-RC522-v2: A simple China made RFID-RC522 Reader; do check the pin labels, as this is a MFRC522 based clone.
  LCD1602-I2C: A standard character display, usually with 2x16 characters. Comes in many colors with LCM1602 IIC attached.
