# Fritzing sketch intrusion-system (saved by Fritzing 0.9.3b)
breadboards: 1

parts:
  U2 = NodeMCU V1.0
  Piezo2 = Piezo Speaker - PC Mount [part_number=COM-07950]
  R2 = Resistor [tolerance=±5% resistance=200 package=THT]
  LED2 = LED - 5mm [color="Blue (470nm)" package="5 mm [THT]"]
  R3 = Resistor [tolerance=±5% resistance=200 package=THT]
  Componente1 = HC-SR501 Body Sensor Module

nets:
  N1: U2.D1, LED2.cathode
  N2: U2.D2, Piezo2.GND
  N3: U2.3V3, R2.Pin_0, R3.Pin_1
  GND: U2.GND, Componente1.GND
  N4: U2.D7, Componente1.OUT
  VIN: U2.Vin, Componente1.VCC
  N5: Piezo2.VCC, R2.Pin_1
  N6: LED2.anode, R3.Pin_0

custom parts:
  NodeMCU V1.0: ESP8266 based NodeMCU
  Piezo Speaker - PC Mount: This is a small 12mm round speaker that operates around the audible 2kHz range. You can use these speakers to create simple music or user interfaces. Each speaker is PTH solderable and requires an operating voltage of 3.5-5V with a mean current of 35mA max. These speakers also have a typical sound output of 95 dBA and a coil resistance of 42 ±6.3 ohms.
  HC-SR501 Body Sensor Module: Pyroelectric Infrared PIR Motion Sensor Detector Module
