# Fritzing sketch light-sensor (saved by Fritzing 0.9.5d)
breadboards: 1

parts:
  U2 = NodeMCU V1.0
  R1 = Photocell (LDR) [package=THT]
  R2 = Resistor [tolerance=±5% resistance=10k package="0805 [SMD]"]
  LED2 = smd LED [color="White (6500K)" package="0805 [SMD]"]
  LED3 = smd LED [color="White (6500K)" package="0805 [SMD]"]
  LED4 = smd LED [color="White (6500K)" package="0805 [SMD]"]
  LED5 = smd LED [color="White (6500K)" package="0805 [SMD]"]
  LED6 = smd LED [color="White (6500K)" package="0805 [SMD]"]
  LED7 = smd LED [color="White (6500K)" package="0805 [SMD]"]
  R3 = Resistor [tolerance=±5% resistance=2.2k package="0805 [SMD]"]
  R4 = Resistor [tolerance=±5% resistance=2.2k package="0805 [SMD]"]
  R5 = Resistor [tolerance=±5% resistance=2.2k package="0805 [SMD]"]
  R6 = Resistor [tolerance=±5% resistance=2.2k package="0805 [SMD]"]
  R7 = Resistor [tolerance=±5% resistance=2.2k package="0805 [SMD]"]
  R8 = Resistor [tolerance=±5% resistance=2.2k package="0805 [SMD]"]

nets:
  N1: U2.D1, LED2.anode
  N2: U2.D2, LED3.anode
  N3: U2.D3, LED4.anode
  N4: U2.3V3, R1.pin_1, R3.Pin_1, R4.Pin_1, R5.Pin_1, R6.Pin_1, R7.Pin_1, R8.Pin_1
  N5: U2.GND, R2.Pin_0
  N6: U2.D5, LED5.anode
  N7: U2.D6, LED6.anode
  N8: U2.D7, LED7.anode
  N9: U2.A0, R1.pin_0, R2.Pin_1
  N10: LED2.cathode, R3.Pin_0
  N11: LED3.cathode, R4.Pin_0
  N12: LED4.cathode, R5.Pin_0
  N13: LED5.cathode, R8.Pin_0
  N14: LED6.cathode, R7.Pin_0
  N15: LED7.cathode, R6.Pin_0

custom parts:
  NodeMCU V1.0: ESP8266 based NodeMCU
